# Fritzing sketch CHEVY (saved by Fritzing 0.8.7b)

parts:
  Part1 = Arduino Mega 2560 (Rev3)
  DC_Motor_Driver = L298N DC motor driver
  DC_Motor_-_RIGHT_WHEEL = DC Motor  # not connected
  M1 = DC Motor [part_number="DC Motor LEFT WHEEL"]  # not connected
  12V_Power_Supply = 18650 battery holder [package=battery-18650-kit]
  BAT2 = 18650 battery holder [package=battery-18650-kit]
  Part2 = KY-033 Line Follower Sensor [package="Breakout board"]
  Line-Tracking_Sensors = KY-033 Line Follower Sensor [package="Breakout board"]
  Part4 = KY-033 Line Follower Sensor [package="Breakout board"]
  Ultrasonic_Sensor = HC-SR04 Ultrasonic Rangemeter
  Front_Lights = LED - 5mm [color="Yellow (595nm)" part_number="Warm White" package="5 mm [THT]"]
  LED2 = LED - 5mm [color="Yellow (595nm)" package="5 mm [THT]"]
  Rear_Lights = Super Flux LED blue [color=Red part_number=SuperFlux]
  LED6 = Super Flux LED blue [color=Red]
  R4 = Resistor [tolerance=±1% resistance=150 package=THT]
  LED7 = Super Flux LED blue [color=Red]
  LED8 = Super Flux LED blue [color=Red]
  R5 = Resistor [tolerance=±1% resistance=150 package=THT]
  R1 = Resistor [tolerance=±1% resistance=150 package=THT]
  R2 = Resistor [tolerance=±1% resistance=150 package=THT]
  HS-422 = Basic Servo
  Push-Button = Pushbutton [package="[THT]"]
  R3 = Resistor [tolerance=±1% resistance=10k package=THT]
  C1 = Ceramic Capacitor [capacitance=100nF voltage=20V package="100 mil [THT, multilayer]"]
  ESP-01_Wifi_Module = ESP8266 ESP01 [part_number=ESP8266 package=THT]
  OLED_128x64_I2C = OLED 128x64 I2C Monochrome Display

nets:
  N1: Part1.D21/SCL, OLED_128x64_I2C.SCK
  N2: Part1.D20/SDA, OLED_128x64_I2C.SDA
  N3: Part1.D19/RX1, ESP-01_Wifi_Module.TXD
  N4: Part1.D18/TX1, ESP-01_Wifi_Module.RXD
  GND: Part1.GND, DC_Motor_Driver.GND, 12V_Power_Supply.-, Part2.GND, Line-Tracking_Sensors.GND, Part4.GND, Ultrasonic_Sensor.GND, R4.Pin_0, R5.Pin_0, R1.Pin_1, R2.Pin_1, HS-422.gnd, R3.Pin_0, C1.0, ESP-01_Wifi_Module.GND, OLED_128x64_I2C.GND
  N5: Part1.D11_PWM, DC_Motor_Driver.IN4
  N6: Part1.D10_PWM, Part2.S
  N7: Part1.D9_PWM, DC_Motor_Driver.IN3
  N8: Part1.D8_PWM, DC_Motor_Driver.IN2
  3V3: Part1.3V3, ESP-01_Wifi_Module.VCC, ESP-01_Wifi_Module.CH_PD, OLED_128x64_I2C.VDD
  VCC: Part1.5V, Part2.V+, Line-Tracking_Sensors.V+, Part4.V+, Ultrasonic_Sensor.VCC, HS-422.vcc, Push-Button.Pin_3
  VIN: Part1.VIN, DC_Motor_Driver.12V, BAT2.+
  N9: Part1.D2_PWM, Part4.S
  N10: Part1.D3_PWM, HS-422.pulse
  N11: Part1.D4_PWM, Line-Tracking_Sensors.S
  N12: Part1.D5_PWM, DC_Motor_Driver.ENA
  N13: Part1.D6_PWM, DC_Motor_Driver.ENB
  N14: Part1.D7_PWM, DC_Motor_Driver.IN1
  N15: Part1.D22, Front_Lights.anode
  N16: Part1.D23, LED2.anode
  N17: Part1.D27, Ultrasonic_Sensor.Trig
  N18: Part1.D29, Ultrasonic_Sensor.Echo
  N19: Part1.D45, Push-Button.Pin_1
  N20: Part1.D52, Rear_Lights.cathode, LED6.cathode
  N21: Part1.D53, LED7.cathode, LED8.cathode
  N22: 12V_Power_Supply.+, BAT2.-
  N23: Front_Lights.cathode, R1.Pin_0
  N24: LED2.cathode, R2.Pin_0
  N25: Rear_Lights.anode, LED6.anode, R4.Pin_1
  N26: LED7.anode, LED8.anode, R5.Pin_1

custom parts:
  L298N DC motor driver: 2x DC motor driver with 78M05 positive voltage regulator (7..35 V) L298N: max 46 V, 2 A Set 5 V Enable jumper to enable 5 V regultor (needed for the L298N) and +5 V output at screw terminal or supply external +5 V at screw terminal Set ENA and/or ENB to +5 V to enable motor permanently or supply ENA and/or ENB with PWM signal IN1 and IN2 set rotation directory for motor A (OUT1/OUT2) IN2 and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
  18650 battery holder: 18650 Battery Holder
  KY-033 Line Follower Sensor: Tracing Black White Line Hunting Sensor Module For Arduino. This is KY-033 tracking sensor. The KY-033 measures the intensity of infrared radiation and delivers it as an analog output voltage. Operating voltage: 2.5 - 12V(cannot over12V), working current: 18mA-20mA at 5V. Enhanced accuracy. Documents: http://www.vishay.com/docs/83760/tcrt5000.pdf
  ESP8266 ESP01: Generic WiFi Module based on the ESP8266 with onboard PCB antenna and UART communications
